# Fritzing sketch TINY_CHARGE-seriesBattery (saved by Fritzing 0.9.1b)
breadboards: 1

parts:
  Part1 = Arduino Uno (Rev3)
  R1 = Resistor [tolerance=±5% resistance=220 package=THT]
  U1 = attiny85 [package=dip]
  NEOPIXEL1 = Neopixel Strip -- White (60/m)
  BAT1 = Battery Holders [package=battery-aa]
  BAT2 = Battery Holders [package=battery-aa]
  NEOPIXEL2 = Neopixel Strip -- White (60/m)
  C3 = Electrolytic Capacitor [capacitance=1000µF package="300 mil [THT, electrolytic]"]
  C4 = Tantalum Capacitor [capacitance=1μF package="200 mil [THT, tantalum]"]
  C5 = Electrolytic Capacitor [capacitance=10μF package="0605 [SMD, electrolytic]"]
  R3 = Resistor [tolerance=±5% resistance=220 package=THT]
  R4 = Resistor [tolerance=±5% resistance=220 package=THT]
  R2 = Resistor [tolerance=±20% resistance=10k package=THT]

nets:
  N1: Part1.D1/TX, R1.Pin_0
  N2: Part1.5V, U1.Pin_8, R2.Pin_0
  GND: Part1.GND, U1.Pin_4, NEOPIXEL1.GND, BAT2.-, C3.-, C5.-
  N3: R1.Pin_1, U1.Pin_2
  N4: U1.Pin_1, R2.Pin_1
  N5: U1.Pin_5, R3.Pin_0
  N6: U1.Pin_7, R4.Pin_0
  N7: NEOPIXEL1.+5V, C3.+, C4.+, C5.+
  N8: BAT1.-, BAT2.+
  N9: BAT1.+, R3.Pin_1
  N10: NEOPIXEL2.DO, R4.Pin_1

notes:
  The pin with a dot like this "." is the pin 1, RESET
  How to connect the parts to the ATTINY85 FOR THE PROGRAM
  A2 to SERIAL
  The ARDUINO is connected to the computer and supply current and a serial connection.
  <= We are here
  to clean the power
  I clean the power ! And I'm fat !
  Capacitors clean the current spikes

custom parts:
  Neopixel Strip -- White (60/m): Neopixel Strip, White, 60 pixels per meter.
